// Logisim project Encoder.circ as structural Verilog: 1 circuit, main circuit main
module main (
  input  x1,
  input  x2,
  input  x3,
  input  x4,
  input  x5,
  input  x6,
  input  x7
);

  wire or_1_out, or_2_out, or_3_out;

  or or_1 (or_1_out, x7, x6, x5, x4);
  or or_2 (or_2_out, x7, x6, x3, x2);
  or or_3 (or_3_out, x7, x5, x3, x1);
  LED led_1 (.in(or_1_out));
  LED led_2 (.in(or_2_out));
  LED led_3 (.in(or_3_out));

  // Notes on the sheet:
  //   Encoder
  //   A2
  //   A!
  //   A0
endmodule
