// Logisim project AND, OR, NOT, NOR, NAND, XOR, Half Adder and Full Adder.circ as structural Verilog: 1 circuit, main circuit main
module main (
  input  in_1,
  input  in_2,
  input  in_3,
  input  in_4,
  input  in_5,
  input  in_6,
  input  in_7,
  input  in_8,
  input  in_9,
  input  in_10,
  input  in_11,
  input  in_12,
  input  in_13,
  input  in_14,
  input  in_15,
  input  in_16
);

  wire and_1_out, and_2_out, and_3_out, and_4_out, and_5_out, and_6_out, and_7_out, and_8_out, nand_1_out,
       nor_1_out, not_1_out, not_2_out, not_3_out, not_4_out, not_5_out, not_6_out, not_7_out, or_1_out,
       or_2_out, or_3_out, or_4_out, xor_1_out, xor_2_out;

  not not_1 (not_1_out, in_8);
  not not_2 (not_2_out, in_9);
  nand nand_1 (nand_1_out, in_12, in_13);
  nor nor_1 (nor_1_out, in_14, in_15);
  LED led_1 (.in(not_3_out));
  not not_3 (not_3_out, in_1);
  LED led_2 (.in(or_1_out));
  or or_1 (or_1_out, in_3, in_4);
  LED led_3 (.in(and_1_out));
  and and_1 (and_1_out, in_6, in_7);
  and and_2 (and_2_out, in_8, not_1_out);
  and and_3 (and_3_out, not_2_out, in_9);
  not not_4 (not_4_out, nand_1_out);
  LED led_4 (.in(not_4_out));
  LED led_5 (.in(not_5_out));
  not not_5 (not_5_out, nor_1_out);
  or or_2 (or_2_out, and_2_out, and_3_out);
  LED led_6 (.in(or_2_out));
  not not_6 (not_6_out, in_5);
  not not_7 (not_7_out, in_2);
  xor xor_1 (xor_1_out, in_10, in_11);
  and and_4 (and_4_out, in_10, in_11);
  and and_5 (and_5_out, in_2, not_6_out);
  and and_6 (and_6_out, not_7_out, in_5);
  and and_7 (and_7_out, in_2, in_5);
  or or_3 (or_3_out, and_5_out, and_6_out);
  LED led_7 (.in(and_7_out));
  xor xor_2 (xor_2_out, xor_1_out, in_16);
  LED led_8 (.in(xor_2_out));
  and and_8 (and_8_out, xor_1_out, in_16);
  LED led_9 (.in(or_3_out));
  LED led_10 (.in(or_4_out));
  or or_4 (or_4_out, and_8_out, and_4_out);

  // Notes on the sheet:
  //   NOT GATE
  //   OR GATE
  //   AND GATE
  //   NAND GATE
  //   NOR GATE
  //   XOR GATE
  //   HALF ADDER
  //   FULL ADDER
endmodule
