// Logisim project Multiplexer.circ as structural Verilog: 1 circuit, main circuit main
module main (
  input  D0,
  input  D1,
  input  D2,
  input  D3,
  input  B,
  input  A
);

  wire and_1_out, and_2_out, and_3_out, and_4_out, not_1_out, not_2_out, or_1_out;

  not not_1 (not_1_out, B);
  not not_2 (not_2_out, A);
  and and_1 (and_1_out, D0, not_1_out, not_2_out);
  and and_2 (and_2_out, D1, not_1_out, A);
  and and_3 (and_3_out, D2, B, not_2_out);
  and and_4 (and_4_out, D3, B, A);
  or or_1 (or_1_out, and_1_out, and_2_out, and_3_out, and_4_out);
  LED led_1 (.in(or_1_out));

  // Notes on the sheet:
  //   Multiplexer
endmodule
